# Fritzing sketch Flasher (saved by Fritzing 1.0.5)
breadboards: 1

parts:
  J1 = longpad pin header, 3 pins [form="long pad"]
  J2 = female pin header, 6 pins [form="♀ (female)"]
  Power_plug1 = Power plug
  S1 = Toggle Switch [package=THT]
  D1 = Rectifier Diode [part_number=1N4001 package="300 mil [THT]"]

nets:
  N1: J1.pin1, S1.COM
  N2: J1.pin2, J2.pin3, D1.cathode
  N3: J1.pin3, J2.pin6, Power_plug1.GND
  N4: J2.pin2, D1.anode
  N5: J2.pin4, S1.L1
  N6: Power_plug1.VCC, S1.L2

notes:
  5V
  UPDI
  GND
  TX
  RX
  External Power <--> Power from USB
